# Fritzing sketch arduino_esp8266 (saved by Fritzing 0.9.3b)
breadboards: 1

parts:
  元件1 = Arduino Mega 2560 (Rev3)
  元件2 = Logic Level Converter
  U1 = Voltage Regulator [package=to220-adj]
  Espessif_Serial_Wifi_Modul_1 = ESP8266 ESP01 [part_number=ESP8266 package=THT]

nets:
  N1: 元件1.D19/RX1, 元件2.TX_HV
  N2: 元件1.D18/TX1, 元件2.TX2_HV
  N3: 元件2.RX2_LV, Espessif_Serial_Wifi_Modul_1.RXD
  N4: 元件2.LV, U1.OUT, Espessif_Serial_Wifi_Modul_1.VCC, Espessif_Serial_Wifi_Modul_1.GPIO16, Espessif_Serial_Wifi_Modul_1.CH_PD
  N5: 元件2.RX_LV, 元件2.TX_LV, Espessif_Serial_Wifi_Modul_1.TXD
  N6: 元件2.HV, U1.IN
  N7: U1.ADJ, Espessif_Serial_Wifi_Modul_1.GND

custom parts:
  ESP8266 ESP01: Generic WiFi Module based on the ESP8266 with onboard PCB antenna and UART communications
